# Fritzing sketch SmartThings Lock (saved by Fritzing 0.9.1b)
breadboards: 1

parts:
  Part1 = Arduino Uno (Rev3)
  Motion_Detector = PIR sensor
  Audible_Feedback = Piezo Speaker
  Door_Feedback = Reed switch [package=THT]
  Lock_Feedback = Reed switch [package=THT]
  Lock_Actuator = Basic Servo

nets:
  N1: Part1.D8, Lock_Feedback.pin_2
  N2: Part1.D9_PWM, Lock_Actuator.pulse
  N3: Part1.D10_PWM/SS, Audible_Feedback.pin2
  N4: Part1.D11_PWM/MOSI, Motion_Detector.SIG
  GND: Part1.GND, Motion_Detector.GND, Audible_Feedback.pin1, Door_Feedback.pin_1, Lock_Feedback.pin_1, Lock_Actuator.gnd
  N5: Part1.D7, Door_Feedback.pin_2
  5V: Part1.5V, Motion_Detector.VDD, Lock_Actuator.vcc
